// Logisim project ULA.circ as structural Verilog: 3 circuits, main circuit main
module main (
  input  [31:0] Entrada_A,
  input  [31:0] Entrada_B,
  input  [4:0] Seletor,
  output out_4,
  output [31:0] \Saída_S 
);

  wire overflowcontroler_1_overflow, undriven, undriven_2, undriven_3, undriven_4, undriven_5, undriven_6,
       undriven_7, undriven_8, undriven_9, undriven_10, undriven_11, undriven_12, undriven_13, undriven_14,
       undriven_15, undriven_16, undriven_17, undriven_18, undriven_19, undriven_20, undriven_21,
       undriven_22, undriven_23, undriven_24, undriven_25, undriven_26, undriven_27, undriven_28,
       undriven_29, undriven_30, undriven_31, undriven_32;

  Celula celula_1 (
    .Cin(undriven), .b(Entrada_B[30]), .a(Entrada_A[30]), .Seletor(Seletor), .S(\Saída_S [30]),
    .Cout(undriven_3));  // open: SLL, SRL
  Celula celula_2 (
    .Cin(undriven_2), .b(Entrada_B[31]), .a(Entrada_A[31]), .Seletor(Seletor), .S(\Saída_S [31]),
    .Cout(undriven));  // open: SLL, SRL
  Celula celula_3 (
    .Cin(undriven_3), .b(Entrada_B[28]), .a(Entrada_A[28]), .Seletor(Seletor), .S(\Saída_S [28]),
    .Cout(undriven_5));  // open: SLL, SRL
  Celula celula_4 (
    .Cin(undriven_4), .b(Entrada_B[29]), .a(Entrada_A[29]), .Seletor(Seletor), .S(\Saída_S [29]),
    .Cout(undriven_2));  // open: SLL, SRL
  Celula celula_5 (
    .Cin(undriven_5), .b(Entrada_B[26]), .a(Entrada_A[26]), .Seletor(Seletor), .S(\Saída_S [26]),
    .Cout(undriven_6));  // open: SLL, SRL
  Celula celula_6 (
    .Cin(undriven_8), .b(Entrada_B[27]), .a(Entrada_A[27]), .Seletor(Seletor), .S(\Saída_S [27]),
    .Cout(undriven_4));  // open: SLL, SRL
  Celula celula_7 (
    .Cin(undriven_6), .b(Entrada_B[24]), .a(Entrada_A[24]), .Seletor(Seletor), .S(\Saída_S [24]),
    .Cout(undriven_9));  // open: SLL, SRL
  Celula celula_8 (
    .Cin(undriven_7), .b(Entrada_B[25]), .a(Entrada_A[25]), .Seletor(Seletor), .S(\Saída_S [25]),
    .Cout(undriven_8));  // open: SLL, SRL
  Celula celula_9 (
    .Cin(undriven_9), .b(Entrada_B[23]), .a(Entrada_A[22]), .Seletor(Seletor), .S(\Saída_S [22]),
    .Cout(undriven_10));  // open: SLL, SRL
  Celula celula_10 (
    .Cin(undriven_11), .b(Entrada_B[22]), .a(Entrada_A[23]), .Seletor(Seletor), .S(\Saída_S [23]),
    .Cout(undriven_7));  // open: SLL, SRL
  Celula celula_11 (
    .Cin(undriven_10), .b(Entrada_B[21]), .a(Entrada_A[20]), .Seletor(Seletor), .S(\Saída_S [20]),
    .Cout(undriven_12));  // open: SLL, SRL
  Celula celula_12 (
    .Cin(undriven_14), .b(Entrada_B[20]), .a(Entrada_A[21]), .Seletor(Seletor), .S(\Saída_S [21]),
    .Cout(undriven_11));  // open: SLL, SRL
  Celula celula_13 (
    .Cin(undriven_12), .b(Entrada_B[19]), .a(Entrada_A[18]), .Seletor(Seletor), .S(\Saída_S [18]),
    .Cout(undriven_13));  // open: SLL, SRL
  Celula celula_14 (
    .Cin(undriven_15), .b(Entrada_B[18]), .a(Entrada_A[19]), .Seletor(Seletor), .S(\Saída_S [19]),
    .Cout(undriven_14));  // open: SLL, SRL
  Celula celula_15 (
    .Cin(undriven_13), .b(Entrada_B[17]), .a(Entrada_A[16]), .Seletor(Seletor), .S(\Saída_S [16]),
    .Cout(undriven_16));  // open: SLL, SRL
  Celula celula_16 (
    .Cin(undriven_18), .b(Entrada_B[16]), .a(Entrada_A[17]), .Seletor(Seletor), .S(\Saída_S [17]),
    .Cout(undriven_15));  // open: SLL, SRL
  Celula celula_17 (
    .Cin(undriven_16), .b(Entrada_B[15]), .a(Entrada_A[14]), .Seletor(Seletor), .S(\Saída_S [14]),
    .Cout(undriven_19));  // open: SLL, SRL
  Celula celula_18 (
    .Cin(undriven_17), .b(Entrada_B[14]), .a(Entrada_A[15]), .Seletor(Seletor), .S(\Saída_S [15]),
    .Cout(undriven_18));  // open: SLL, SRL
  Celula celula_19 (
    .Cin(undriven_19), .b(Entrada_B[13]), .a(Entrada_A[12]), .Seletor(Seletor), .S(\Saída_S [12]),
    .Cout(undriven_21));  // open: SLL, SRL
  Celula celula_20 (
    .Cin(undriven_20), .b(Entrada_B[12]), .a(Entrada_A[13]), .Seletor(Seletor), .S(\Saída_S [13]),
    .Cout(undriven_17));  // open: SLL, SRL
  Celula celula_21 (
    .Cin(undriven_21), .b(Entrada_B[11]), .a(Entrada_A[10]), .Seletor(Seletor), .S(\Saída_S [10]),
    .Cout(undriven_22));  // open: SLL, SRL
  Celula celula_22 (
    .Cin(undriven_25), .b(Entrada_B[10]), .a(Entrada_A[11]), .Seletor(Seletor), .S(\Saída_S [11]),
    .Cout(undriven_20));  // open: SLL, SRL
  Celula celula_23 (
    .Cin(undriven_22), .b(Entrada_B[9]), .a(Entrada_A[8]), .Seletor(Seletor), .S(\Saída_S [8]),
    .Cout(undriven_24));  // open: SLL, SRL
  Celula celula_24 (
    .Cin(undriven_23), .b(Entrada_B[8]), .a(Entrada_A[9]), .Seletor(Seletor), .S(\Saída_S [9]),
    .Cout(undriven_25));  // open: SLL, SRL
  Celula celula_25 (
    .Cin(undriven_24), .b(Entrada_B[7]), .a(Entrada_A[6]), .Seletor(Seletor), .S(\Saída_S [6]),
    .Cout(undriven_26));  // open: SLL, SRL
  Celula celula_26 (
    .Cin(undriven_27), .b(Entrada_B[6]), .a(Entrada_A[7]), .Seletor(Seletor), .S(\Saída_S [7]),
    .Cout(undriven_23));  // open: SLL, SRL
  Celula celula_27 (
    .Cin(undriven_26), .b(Entrada_B[5]), .a(Entrada_A[4]), .Seletor(Seletor), .S(\Saída_S [4]),
    .Cout(undriven_28));  // open: SLL, SRL
  Celula celula_28 (
    .Cin(undriven_30), .b(Entrada_B[4]), .a(Entrada_A[5]), .Seletor(Seletor), .S(\Saída_S [5]),
    .Cout(undriven_27));  // open: SLL, SRL
  Celula celula_29 (
    .Cin(undriven_28), .b(Entrada_B[3]), .a(Entrada_A[2]), .Seletor(Seletor), .S(\Saída_S [2]),
    .Cout(undriven_29));  // open: SLL, SRL
  Celula celula_30 (
    .Cin(undriven_32), .b(Entrada_B[2]), .a(Entrada_A[3]), .Seletor(Seletor), .S(\Saída_S [3]),
    .Cout(undriven_30));  // open: SLL, SRL
  Celula celula_31 (
    .Cin(undriven_29), .b(Entrada_B[1]), .a(Entrada_A[0]), .Seletor(Seletor), .S(\Saída_S [0]),
    .Cout(undriven_31));  // open: SLL, SRL
  Celula celula_32 (
    .Cin(1'b0), .b(Entrada_B[0]), .a(Entrada_A[1]), .Seletor(Seletor), .S(\Saída_S [1]), .Cout(undriven_32));  // open: SLL, SRL
  OverFlowControler overflowcontroler_1 (
    .Overflow(overflowcontroler_1_overflow), .Cin(undriven_31), .Seletor(Seletor), .a(Entrada_A[0]),
    .b(Entrada_B[1]), .s(\Saída_S [0]));

  // Notes on the sheet:
  //   00000=AND
  //   00001=OR
  //   00010=XOR
  //   00011=NAND
  //   00100=SOMA INT
  //   00101=SOMA NAT
  //   00110=SUBTRAIR
  //   Overflow
endmodule

module Celula (
  input  Cin,
  input  SLL,
  input  SRL,
  input  b,
  input  a,
  input  Cout,
  input  [4:0] Seletor,
  output S
);

  wire adder_1_cout, adder_1_out, and_1_out, and_2_out, nand_1_out, or_1_out, subtractor_1_bout,
       subtractor_1_out, xor_1_out;

  and and_1 (and_1_out, a, b);
  or or_1 (or_1_out, a, b);
  xor xor_1 (xor_1_out, a, b);
  nand nand_1 (nand_1_out, a, b);
  Adder #(.width(1)) adder_1 (.a(a), .b(b), .out(adder_1_out), .cin(Cin), .cout(adder_1_cout));
  Subtractor #(.width(1)) subtractor_1 (.a(a), .b(b), .out(subtractor_1_out), .bin(Cin), .bout(subtractor_1_bout));
  Multiplexer #(.enable("false")) multiplexer_1 (
    .in0(adder_1_cout), .in1(subtractor_1_bout), .out(Cout), .sel(and_2_out));
  and and_2 (and_2_out, ~Seletor[0], Seletor[1], Seletor[2], ~Seletor[3], ~Seletor[4]);  // AND_Gate
  Multiplexer #(.select(5), .enable("false")) multiplexer_2 (
    .in0(and_1_out), .in1(or_1_out), .in2(xor_1_out), .in3(nand_1_out), .in4(adder_1_out), .in5(adder_1_out),
    .in6(subtractor_1_out), .in7(SLL), .in8(SRL), .out(S), .sel(Seletor));  // open: in9, in10, in11, in12, in13, in14, in15, in16, in17, in18, in19, in20, in21, in22, in23, in24, in25, in26, in27, in28, in29, in30, in31

  // Notes on the sheet:
  //   00000=AND
  //   00001=OR
  //   00010=XOR
  //   00011=NAND
  //   00100=SOMA INT
  //   00101=SOMA NAT
  //   00110=SUBTRATOR
  //   00111=DESLOCAMENTO ESQUERDA
  //   01000=DESLOCAMENTO DIREITA
endmodule

module OverFlowControler (
  input  Cin,
  input  a,
  input  b,
  input  s,
  input  [4:0] Seletor,
  output Overflow
);

  wire and_1_out, and_2_out, and_3_out, or_1_out;

  Multiplexer #(.enable("false")) multiplexer_1 (.in0(Cin), .in1(or_1_out), .out(Overflow), .sel(and_1_out));
  and and_1 (and_1_out, Seletor[0], ~Seletor[1], Seletor[2], ~Seletor[3], ~Seletor[4]);  // AND_Gate
  or or_1 (or_1_out, and_2_out, and_3_out);
  and and_2 (and_2_out, a, b, ~s);  // AND_Gate
  and and_3 (and_3_out, ~a, ~b, s);  // AND_Gate

  // Notes on the sheet:
  //   00100 - Soma de Naturais
  //   00101 - Soma de Inteiros
endmodule
